# Fritzing sketch play (saved by Fritzing 0.9.4)
perfboards: 2

parts:
  TP-00-C3 = TTP223 Touch Module [part_number=TTP223]
  TP-04-E3 = TTP223 Touch Module [part_number=TTP223]
  TP-02-D3 = TTP223 Touch Module [part_number=TTP223]
  TP-01-C3S = TTP223 Touch Module [part_number=TTP223]
  TP-03-D3S = TTP223 Touch Module [part_number=TTP223]
  TP-05-F3 = TTP223 Touch Module [part_number=TTP223]
  TP-07-G3 = TTP223 Touch Module [part_number=TTP223]
  TP-09-A3 = TTP223 Touch Module [part_number=TTP223]
  TP-11-B3 = TTP223 Touch Module [part_number=TTP223]
  TP-06-F3S = TTP223 Touch Module [part_number=TTP223]
  TP-08-G3S = TTP223 Touch Module [part_number=TTP223]
  TP-10-A3S = TTP223 Touch Module [part_number=TTP223]
  MUX0 = 74HC4051 [package="DIP (Dual Inline) [THT]"]
  MUX1 = 74HC4051 [package="DIP (Dual Inline) [THT]"]
  MUX2 = 74HC4051 [package="DIP (Dual Inline) [THT]"]
  TP-22-A4S = TTP223 Touch Module [part_number=TTP223]
  TP-20-G4S = TTP223 Touch Module [part_number=TTP223]
  TP-18-F4S = TTP223 Touch Module [part_number=TTP223]
  TP-23-B4 = TTP223 Touch Module [part_number=TTP223]
  TP-21-A4 = TTP223 Touch Module [part_number=TTP223]
  TP-19-G4 = TTP223 Touch Module [part_number=TTP223]
  TP-17-F4 = TTP223 Touch Module [part_number=TTP223]
  TP-15-D4S = TTP223 Touch Module [part_number=TTP223]
  TP-13-C4S = TTP223 Touch Module [part_number=TTP223]
  TP-14-D4 = TTP223 Touch Module [part_number=TTP223]
  TP-16-E4 = TTP223 Touch Module [part_number=TTP223]
  TP-12-C4 = TTP223 Touch Module [part_number=TTP223]
  TP-24-C5 = TTP223 Touch Module [part_number=TTP223]
  AMP8403 = GF1002 Stereo Amplifier
  SPEAKER = SPEAKER [package=pcb_mount_speaker]
  BTN-REC = Pushbutton [package="[THT]"]
  BTN-INS = Pushbutton [package="[THT]"]
  BTN-PLAY = Pushbutton [package="[THT]"]
  R-10K-POWER = Resistor [tolerance=±5% resistance=10k package="0805 [SMD]"]
  R-220-PLAY = Resistor [tolerance=±5% resistance=220 package="0805 [SMD]"]
  R-220-REC = Resistor [tolerance=±5% resistance=220 package="0805 [SMD]"]
  LED-REC = smd LED [color="Red (633nm)" package="0603 [SMD]"]
  LED-POWER = smd LED [color="White (4500K)" package="0603 [SMD]"]
  LED-PLAY = smd LED [color="Green (570nm)" package="0603 [SMD]"]
  MUX3 = 74HC4051 [package="DIP (Dual Inline) [THT]"]
  MCU1 = Raspberry Pi Zero

nets:
  GND: TP-00-C3.GND, TP-04-E3.GND, TP-02-D3.GND, TP-01-C3S.GND, TP-03-D3S.GND, TP-05-F3.GND, TP-07-G3.GND, TP-09-A3.GND, TP-11-B3.GND, TP-06-F3S.GND, TP-08-G3S.GND, TP-10-A3S.GND, MUX0.INH, MUX0.VEE, MUX0.VSS, MUX1.INH, MUX1.VEE, MUX1.VSS, MUX2.INH, MUX2.VEE, MUX2.VSS, TP-22-A4S.GND, TP-20-G4S.GND, TP-18-F4S.GND, TP-23-B4.GND, TP-21-A4.GND, TP-19-G4.GND, TP-17-F4.GND, TP-15-D4S.GND, TP-13-C4S.GND, TP-14-D4.GND, TP-16-E4.GND, TP-12-C4.GND, TP-24-C5.GND, AMP8403.POWER-, AMP8403.INPUTG, R-10K-POWER.Pin_1, R-220-PLAY.Pin_1, R-220-REC.Pin_1, MUX3.INH, MUX3.VEE, MUX3.VSS, MCU1.pin_6, MCU1.pin_9, MCU1.pin_14, MCU1.pin_25, MCU1.pin_34, MCU1.pin_39
  N1: TP-00-C3.I/O, MUX0.IO4
  VCC: TP-00-C3.VCC, TP-04-E3.VCC, TP-02-D3.VCC, TP-01-C3S.VCC, TP-03-D3S.VCC, TP-05-F3.VCC, TP-07-G3.VCC, TP-09-A3.VCC, TP-11-B3.VCC, TP-06-F3S.VCC, TP-08-G3S.VCC, TP-10-A3S.VCC, MUX0.VDD, MUX1.VDD, MUX2.VDD, TP-22-A4S.VCC, TP-20-G4S.VCC, TP-18-F4S.VCC, TP-23-B4.VCC, TP-21-A4.VCC, TP-19-G4.VCC, TP-17-F4.VCC, TP-15-D4S.VCC, TP-13-C4S.VCC, TP-14-D4.VCC, TP-16-E4.VCC, TP-12-C4.VCC, TP-24-C5.VCC, MUX3.VDD, MCU1.pin_2, MCU1.pin_4
  N2: TP-04-E3.I/O, MUX0.IO3
  N3: TP-02-D3.I/O, MUX0.IO7
  N4: TP-01-C3S.I/O, MUX0.IO6
  N5: TP-03-D3S.I/O, MUX0.IO5
  N6: TP-05-F3.I/O, MUX0.IO0
  N7: TP-07-G3.I/O, MUX0.IO2
  N8: TP-09-A3.I/O, MUX1.IO6
  N9: TP-11-B3.I/O, MUX1.IO5
  N10: TP-06-F3S.I/O, MUX0.IO1
  N11: TP-08-G3S.I/O, MUX1.IO4
  N12: TP-10-A3S.I/O, MUX1.IO7
  N13: MUX0.IO, MCU1.pin_29
  N14: MUX0.C, MUX1.C, MUX2.C, MUX3.C, MCU1.pin_11
  N15: MUX0.B, MUX1.B, MUX2.B, MUX3.B, MCU1.pin_13
  N16: MUX0.A, MUX1.A, MUX2.A, MUX3.A, MCU1.pin_15
  N17: MUX1.IO, MCU1.pin_31
  N18: MUX1.IO1, TP-12-C4.I/O
  N19: MUX1.IO2, TP-13-C4S.I/O
  N20: MUX2.IO4, TP-14-D4.I/O
  N21: MUX2.IO6, TP-15-D4S.I/O
  N22: MUX2.IO, MCU1.pin_33
  N23: MUX2.IO7, TP-16-E4.I/O
  N24: MUX2.IO3, TP-17-F4.I/O
  N25: MUX2.IO0, TP-18-F4S.I/O
  N26: MUX2.IO1, TP-19-G4.I/O
  N27: MUX2.IO2, TP-20-G4S.I/O
  N28: TP-22-A4S.I/O, MUX3.IO6
  N29: TP-23-B4.I/O, MUX3.IO7
  N30: TP-21-A4.I/O, MUX3.IO4
  N31: TP-24-C5.I/O, MUX3.IO5
  N32: AMP8403.LOUT+, SPEAKER.+
  N33: AMP8403.LOUT-, SPEAKER.-
  N34: AMP8403.POWER+, BTN-REC.Pin_3, BTN-REC.Pin_4, BTN-INS.Pin_3, BTN-INS.Pin_4, BTN-PLAY.Pin_3, BTN-PLAY.Pin_4, LED-POWER.cathode, MCU1.pin_1, MCU1.pin_17
  N35: AMP8403.INPUTL, MCU1.pin_12
  N36: BTN-REC.Pin_1, BTN-REC.Pin_2, MCU1.pin_32
  N37: BTN-INS.Pin_1, BTN-INS.Pin_2, MCU1.pin_36
  N38: BTN-PLAY.Pin_1, BTN-PLAY.Pin_2, MCU1.pin_38
  N39: R-10K-POWER.Pin_0, LED-POWER.anode
  N40: R-220-PLAY.Pin_0, LED-PLAY.anode
  N41: R-220-REC.Pin_0, LED-REC.anode
  N42: LED-REC.cathode, MCU1.pin_40
  N43: LED-PLAY.cathode, MCU1.pin_37
  N44: MUX3.IO, MCU1.pin_35

custom parts:
  TTP223 Touch Module: Single touch module. Other side has "A" "B" terminal to short and use "AHLB" & "Toggle" Mode.
  74HC4051: 8 channel analog multiplexer/demultiplexer
  GF1002 Stereo Amplifier: GF1002 6 Watt Stereo Amplifier
